# Fritzing sketch OfficialFritzingDiagram (saved by Fritzing 1.0.3b)
breadboards: 1

parts:
  U2 = LIPO-2000mAh [package=lipo-2000]
  A2 = DHT22 module
  J2 = Piezo Speaker
  MOTOR2 = Vibration Motor
  Part6 = Adafruit BNO055 STEMMA QT [part_number="Adafruit #4646"]
  R1 = Resistor [tolerance=±5% power=0.25W resistance=10k package=THT]
  Part2 = Adafruit Feather HUZZAH ESP8266 [part_number="Adafruit #2821"]

nets:
  VCC: U2.+, A2.+, Part6.VCC, Part2.3.3V
  GND: U2.-, A2.-, J2.pin1, MOTOR2.NEG, Part6.GND, Part2.GND
  N1: A2.Out, R1.Pin_0
  N2: MOTOR2.POS, Part2.GPIO13/MOSI
  N3: Part6.SCL, Part2.GPIO5/SCL
  N4: Part6.SDA, Part2.GPIO4/SDA
  N5: R1.Pin_1, Part2.GPIO14/SCK

notes:
  ESP8266
  3V : positive rail breadboard
  GND : negative rail breadboard
  SCL : SCL BNO055
  SDA : SDA BNO055
  GPIO 14 : out DHT22
  GPIO 12 : + Buzzer
  GPIO 13 : + Vibration
  BNO055 Orientation Sensor
  VCC : positive rail breadboard
  GND : negative rail breadboard
  SCL : GPIO 5 (SCL Microcontroller)
  SDA : GPIO 4 (SDA Microcontroller)
  DHT22 Temperature/Humidity Sensor
  + : positive rail breadboard
  output : GPIO pin 14 (Microcontroller)
  - : negative rail breadboard
  Vibration Motor
  + : GPIO 13 (Microcontroller)
  - : negative rail breadboard
  Piezo Buzzer
  + : GPIO 12 (microcontroller)
  - : negative rail breadboard

custom parts:
  DHT22 module: DHT22 module. Pins VCC Data GND.
  Vibration Motor: An eccentric vibration motor!
  Adafruit BNO055 STEMMA QT: If you've ever ordered and wire up a 9-DOF sensor, chances are you've also realized the challenge of turning the sensor data from an accelerometer, gyroscope, and magnetometer into actual "3D space orientation"! Orientation is a hard problem to solve. The sensor fusion algorithms (the secret sauce that blends accelerometer, magnetometer, and gyroscope data into stable three-axis orientation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
  Adafruit Feather HUZZAH ESP8266: his is the Adafruit Feather HUZZAH ESP8266 - our take on an 'all-in-one' ESP8266 WiFi development board with built in USB and battery charging. Its an ESP8266 WiFi module with all the extras you need, ready to rock! We have other boards in the Feather family, check'em out here. At the Feather HUZZAH's heart is an ESP8266 WiFi microcontroller clocked at 80 MHz and at 3.3V logic. This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
